# Fritzing sketch ESP32 Thing schema (saved by Fritzing 0.9.3b)
breadboards: 1

parts:
  LED1 = LED - 5mm [color="Red (633nm)" package="5 mm [THT]"]
  BTN_1 = Round Pushbutton
  BTN2 = Round Pushbutton
  S8 = Square Pushbutton
  BTN_3 = Round Pushbutton
  BTN_4 = Round Pushbutton
  Part1 = HX711 Weighing Sensor Module
  S11 = Reed switch [package=THT]
  U1 = RELAY [package=relay-jzc]  # not connected
  J2 = JST-B3P-VH [part_number=JST-B3P-VH package=THT]  # not connected
  U2 = RELAY [package=relay-jzc]  # not connected
  U3 = RELAY [package=relay-jzc]  # not connected
  U4 = RELAY [package=relay-jzc]  # not connected
  R1 = Resistor [tolerance=±5% resistance=4.7k package=THT]
  R2 = Resistor [tolerance=±5% resistance=4.7k package=THT]
  Part2 = Arduino Uno (Rev3)
  Grove1 = Grove 4 Digit Display  # not connected
  R3 = Resistor [tolerance=±5% resistance=220 package=THT]
  J3 = Piezo Speaker
  R4 = Resistor [tolerance=±5% resistance=220 package=THT]
  R5 = Resistor [tolerance=±5% resistance=220 package=THT]
  R6 = Resistor [tolerance=±5% resistance=220 package=THT]

nets:
  GND: LED1.cathode, Part1.GND, R1.Pin_1, R2.Pin_1, Part2.GND, R3.Pin_1, J3.pin1
  N1: LED1.anode, Part2.D5_PWM, J3.pin2
  N2: BTN_1.leg0, R2.Pin_0, Part2.D12/MISO
  VCC: BTN_1.leg1, BTN2.leg1, S8.leg1, BTN_3.leg1, BTN_4.leg1, Part1.VCC, S11.pin_1, Part2.D4, Part2.5V
  N3: BTN2.leg0, R1.Pin_0, Part2.D13/SCK
  N4: S8.leg0, R6.Pin_0
  N5: BTN_3.leg0, Part2.D6_PWM, R4.Pin_1
  N6: BTN_4.leg0, Part2.D7, R5.Pin_1
  N7: Part1.DO/RX, Part2.D0/RX
  N8: Part1.CK/TX, Part2.D1/TX
  N9: S11.pin_2, Part2.D2, R3.Pin_0
  N10: R4.Pin_0, R5.Pin_0, R6.Pin_1
